# Fritzing sketch StepperClockCopal (saved by Fritzing 0.9.9b)
breadboards: 1

parts:
  Part2 = Arduino Nano (Rev3.0)
  ZS-042_RTC1 = ZS-042 RTC Module
  BREAKOUT1 = ULN2003A breakout board
  J1 = Piezo Speaker
  LED1 = LED - 5mm [color="Red (633nm)" current=0.030 part_number="Orange front-light LED" package="5 mm [THT]"]
  S1 = Pushbutton [part_number="Manual Advance Button" package=THT]
  S2 = Toggle Switch [part_number="Alarm microswitch" package=THT]
  R1 = Resistor [tolerance=±5% resistance=220 package="0402 [SMD]"]

nets:
  GND: Part2.GND, ZS-042_RTC1.GND, BREAKOUT1.0V, J1.pin1, LED1.cathode, S1.leg1, S2.L1
  N1: Part2.D2, S1.leg0
  N2: Part2.D3, ZS-042_RTC1.SQW
  N3: Part2.D4, S2.COM
  N4: Part2.D5, R1.Pin_1
  N5: Part2.D6, J1.pin2
  N6: Part2.D9, BREAKOUT1.In_4
  N7: Part2.D10, BREAKOUT1.In_3
  N8: Part2.D11/MOSI, BREAKOUT1.In_2
  N9: Part2.D12/MISO, BREAKOUT1.In_1
  5V: Part2.5V, ZS-042_RTC1.VCC, BREAKOUT1.+5V
  N10: Part2.A5, ZS-042_RTC1.SCL
  N11: Part2.A4, ZS-042_RTC1.SDA
  N12: LED1.anode, R1.Pin_0

custom parts:
  ULN2003A breakout board: ULN2003A 7-way Darlington Transistor Driver on breakoutboard
